# Fritzing sketch schema_platine (saved by Fritzing 0.9.3b)
breadboards: 1

parts:
  Composant1 = Arduino Nano (Rev3.0)
  Composant3 = LED Matrix - Serial Interface - Red/Green/Blue  # not connected
  Composant2 = LED Matrix - Serial Interface - Red/Green/Blue
  Composant4 = LED Matrix - Serial Interface - Red/Green/Blue  # not connected
  Composant5 = LED Matrix - Serial Interface - Red/Green/Blue  # not connected
  Composant6 = Bluetooth HC-05 Macho
  Composant7 = Real Time Clock Module - DS1307 RTC Breakout Board

nets:
  GND: Composant1.GND, Composant2.SCK, Composant6.GND, Composant7.GND
  N1: Composant1.D7, Composant7.SDA
  N2: Composant1.D8, Composant7.SCL
  N3: Composant1.D9, Composant6.TXD
  N4: Composant1.D10, Composant6.RXD
  N5: Composant1.D11/MOSI, Composant2.MOSI
  N6: Composant1.D12/MISO, Composant2.GND
  5V: Composant1.5V, Composant2.VCC, Composant6.VCC, Composant7.5V
  N7: Composant1.D13/SCK, Composant2.CS

notes:
  GND
  VCC
  DIN
  CS
  CLK
